// Logisim project main.circ as structural Verilog: 1 circuit, main circuit main
module main (
);

  wire clock_1_out, clock_2_out;
  wire [7:0] A_q, adder_1_out, adder_2_out, bit_extender_1_out, multiplexer_1_out, multiplexer_2_out,
       multiplexer_3_out, multiplier_1_out, PC_q, rom_1_data;

  Register PC (.D(multiplexer_1_out), .clk(clock_1_out), .Q(PC_q));  // open: en, clr
  Multiplexer #(.width(8)) multiplexer_1 (
    .in0(adder_1_out), .in1(bit_extender_1_out), .out(multiplexer_1_out), .sel(rom_1_data[7]));
  Clock clock_1 (.out(clock_1_out));
  ROM rom_1 (.addr(PC_q), .data(rom_1_data));
  Adder adder_1 (.a(8'h1), .b(PC_q), .out(adder_1_out));  // open: cin, cout
  assign bit_extender_1_out = {{2{rom_1_data[5]}}, rom_1_data[5:0]};  // Bit_Extender bit_extender_1
  Adder adder_2 (.a(A_q), .b(bit_extender_1_out), .out(adder_2_out));  // open: cin, cout
  Multiplier multiplier_1 (.a(A_q), .b(bit_extender_1_out), .out(multiplier_1_out));  // open: cin, cout
  Multiplexer #(.width(8)) multiplexer_2 (
    .in0(adder_2_out), .in1(multiplier_1_out), .out(multiplexer_2_out), .sel(rom_1_data[6]));
  Register A (.D(multiplexer_3_out), .clk(clock_2_out), .Q(A_q));  // open: en, clr
  Multiplexer #(.width(8)) multiplexer_3 (
    .in0(multiplexer_2_out), .in1(bit_extender_1_out), .out(multiplexer_3_out), .sel(rom_1_data[7]));
  Clock clock_2 (.out(clock_2_out));

  // Notes on the sheet:
  //   contents of rom_1 (hex, n*v repeats v):
  //   c2 42 42 42 c0 80
endmodule
