// Logisim project fetch.circ as structural Verilog: 1 circuit, main circuit main
module main (
);

  wire clock_1_out;
  wire [7:0] IM_p2, IM_p3, IM_p4, IM_p5;
  wire [31:0] adder_1_out, PC_q;

  Register #(.width(32)) PC (.D(adder_1_out), .clk(clock_1_out), .Q(PC_q));  // open: en, clr
  Clock clock_1 (.out(clock_1_out));
  Adder #(.width(32)) adder_1 (.a(32'h4), .b(PC_q), .out(adder_1_out));  // open: cin, cout
  // ROM #(.addrWidth(24), .line("quad")) IM: pin names not known; wires that end beside it: PC_q[23:0], IM_p2, IM_p3, IM_p4, IM_p5

  // Notes on the sheet:
  //   PC + 4
  //   Instruction
endmodule
