// Logisim project regfile.circ as structural Verilog: 1 circuit, main circuit main
module main (
  input  [4:0] R1,
  input  [4:0] R2,
  input  [4:0] WR,
  input  [31:0] WD,
  input  RegWrite,
  output [31:0] D1,
  output [31:0] D2
);

  wire clock_1_out, clock_2_out, clock_3_out, clock_4_out, clock_5_out, clock_6_out, clock_7_out,
       clock_8_out, clock_9_out, clock_10_out, clock_11_out, clock_12_out, clock_13_out, clock_14_out,
       clock_15_out, clock_16_out, clock_17_out, clock_18_out, clock_19_out, clock_20_out, clock_21_out,
       clock_22_out, clock_23_out, clock_24_out, clock_25_out, clock_26_out, clock_27_out, clock_28_out,
       clock_29_out, clock_30_out, clock_31_out, clock_32_out, WE1, WE2, WE3, WE4, WE5, WE6, WE7, WE8, WE9,
       WE10, WE11, WE12, WE13, WE14, WE15, WE16, WE17, WE18, WE19, WE20, WE21, WE22, WE23, WE24, WE25, WE26,
       WE27, WE28, WE29, WE30, WE31;
  wire [31:0] Q0, Q1, Q2, Q3, Q4, Q5, Q6, Q7, Q8, Q9, Q10, Q11, Q12, Q13, Q14, Q15, Q16, Q17, Q18, Q19, Q20,
       Q21, Q22, Q23, Q24, Q25, Q26, Q27, Q28, Q29, Q30, Q31;

  Demultiplexer #(.select(5)) demultiplexer_1 (
    .out1(WE1), .out2(WE2), .out3(WE3), .out4(WE4), .out5(WE5), .out6(WE6), .out7(WE7), .out8(WE8),
    .out9(WE9), .out10(WE10), .out11(WE11), .out12(WE12), .out13(WE13), .out14(WE14), .out15(WE15),
    .out16(WE16), .out17(WE17), .out18(WE18), .out19(WE19), .out20(WE20), .out21(WE21), .out22(WE22),
    .out23(WE23), .out24(WE24), .out25(WE25), .out26(WE26), .out27(WE27), .out28(WE28), .out29(WE29),
    .out30(WE30), .out31(WE31), .in(RegWrite), .sel(WR));  // open: out0
  Register #(.width(32)) zero (.D(WD), .clk(clock_1_out), .Q(Q0));  // open: en, clr
  Clock clock_1 (.out(clock_1_out));
  Register #(.width(32)) a0 (.D(WD), .en(WE4), .clk(clock_2_out), .Q(Q4));  // open: clr
  Clock clock_2 (.out(clock_2_out));
  Register #(.width(32)) t0 (.D(WD), .en(WE8), .clk(clock_3_out), .Q(Q8));  // open: clr
  Clock clock_3 (.out(clock_3_out));
  Register #(.width(32)) t4 (.D(WD), .en(WE12), .clk(clock_4_out), .Q(Q12));  // open: clr
  Clock clock_4 (.out(clock_4_out));
  Register #(.width(32)) s0 (.D(WD), .en(WE16), .clk(clock_5_out), .Q(Q16));  // open: clr
  Clock clock_5 (.out(clock_5_out));
  Register #(.width(32)) s4 (.D(WD), .en(WE20), .clk(clock_6_out), .Q(Q20));  // open: clr
  Clock clock_6 (.out(clock_6_out));
  Register #(.width(32)) t8 (.D(WD), .en(WE24), .clk(clock_7_out), .Q(Q24));  // open: clr
  Clock clock_7 (.out(clock_7_out));
  Register #(.width(32)) gp (.D(WD), .en(WE28), .clk(clock_8_out), .Q(Q28));  // open: clr
  Clock clock_8 (.out(clock_8_out));
  Register #(.width(32)) at (.D(WD), .en(WE1), .clk(clock_9_out), .Q(Q1));  // open: clr
  Clock clock_9 (.out(clock_9_out));
  Register #(.width(32)) a1 (.D(WD), .en(WE5), .clk(clock_10_out), .Q(Q5));  // open: clr
  Clock clock_10 (.out(clock_10_out));
  Register #(.width(32)) t1 (.D(WD), .en(WE9), .clk(clock_11_out), .Q(Q9));  // open: clr
  Clock clock_11 (.out(clock_11_out));
  Register #(.width(32)) t5 (.D(WD), .en(WE13), .clk(clock_12_out), .Q(Q13));  // open: clr
  Clock clock_12 (.out(clock_12_out));
  Register #(.width(32)) s1 (.D(WD), .en(WE17), .clk(clock_13_out), .Q(Q17));  // open: clr
  Clock clock_13 (.out(clock_13_out));
  Register #(.width(32)) s5 (.D(WD), .en(WE21), .clk(clock_14_out), .Q(Q21));  // open: clr
  Clock clock_14 (.out(clock_14_out));
  Register #(.width(32)) t9 (.D(WD), .en(WE25), .clk(clock_15_out), .Q(Q25));  // open: clr
  Clock clock_15 (.out(clock_15_out));
  Register #(.width(32)) sp (.D(WD), .en(WE29), .clk(clock_16_out), .Q(Q29));  // open: clr
  Clock clock_16 (.out(clock_16_out));
  Register #(.width(32)) v0 (.D(WD), .en(WE2), .clk(clock_17_out), .Q(Q2));  // open: clr
  Clock clock_17 (.out(clock_17_out));
  Register #(.width(32)) a2 (.D(WD), .en(WE6), .clk(clock_18_out), .Q(Q6));  // open: clr
  Clock clock_18 (.out(clock_18_out));
  Register #(.width(32)) t2 (.D(WD), .en(WE10), .clk(clock_19_out), .Q(Q10));  // open: clr
  Clock clock_19 (.out(clock_19_out));
  Register #(.width(32)) t6 (.D(WD), .en(WE14), .clk(clock_20_out), .Q(Q14));  // open: clr
  Clock clock_20 (.out(clock_20_out));
  Register #(.width(32)) s2 (.D(WD), .en(WE18), .clk(clock_21_out), .Q(Q18));  // open: clr
  Clock clock_21 (.out(clock_21_out));
  Register #(.width(32)) s6 (.D(WD), .en(WE22), .clk(clock_22_out), .Q(Q22));  // open: clr
  Clock clock_22 (.out(clock_22_out));
  Register #(.width(32)) k0 (.D(WD), .en(WE26), .clk(clock_23_out), .Q(Q26));  // open: clr
  Clock clock_23 (.out(clock_23_out));
  Register #(.width(32)) fp (.D(WD), .en(WE30), .clk(clock_24_out), .Q(Q30));  // open: clr
  Clock clock_24 (.out(clock_24_out));
  Register #(.width(32)) v1 (.D(WD), .en(WE3), .clk(clock_25_out), .Q(Q3));  // open: clr
  Clock clock_25 (.out(clock_25_out));
  Register #(.width(32)) a3 (.D(WD), .en(WE7), .clk(clock_26_out), .Q(Q7));  // open: clr
  Clock clock_26 (.out(clock_26_out));
  Register #(.width(32)) t3 (.D(WD), .en(WE11), .clk(clock_27_out), .Q(Q11));  // open: clr
  Clock clock_27 (.out(clock_27_out));
  Register #(.width(32)) t7 (.D(WD), .en(WE15), .clk(clock_28_out), .Q(Q15));  // open: clr
  Clock clock_28 (.out(clock_28_out));
  Register #(.width(32)) s3 (.D(WD), .en(WE19), .clk(clock_29_out), .Q(Q19));  // open: clr
  Clock clock_29 (.out(clock_29_out));
  Register #(.width(32)) s7 (.D(WD), .en(WE23), .clk(clock_30_out), .Q(Q23));  // open: clr
  Clock clock_30 (.out(clock_30_out));
  Register #(.width(32)) k1 (.D(WD), .en(WE27), .clk(clock_31_out), .Q(Q27));  // open: clr
  Clock clock_31 (.out(clock_31_out));
  Register #(.width(32)) ra (.D(WD), .en(WE31), .clk(clock_32_out), .Q(Q31));  // open: clr
  Clock clock_32 (.out(clock_32_out));
  Multiplexer #(.select(5), .width(32)) multiplexer_1 (
    .in0(Q0), .in1(Q1), .in2(Q2), .in3(Q3), .in4(Q4), .in5(Q5), .in6(Q6), .in7(Q7), .in8(Q8), .in9(Q9),
    .in10(Q10), .in11(Q11), .in12(Q12), .in13(Q13), .in14(Q14), .in15(Q15), .in16(Q16), .in17(Q17),
    .in18(Q18), .in19(Q19), .in20(Q20), .in21(Q21), .in22(Q22), .in23(Q23), .in24(Q24), .in25(Q25),
    .in26(Q26), .in27(Q27), .in28(Q28), .in29(Q29), .in30(Q30), .in31(Q31), .out(D1), .sel(R1));
  Multiplexer #(.select(5), .width(32)) multiplexer_2 (
    .in0(Q0), .in1(Q1), .in2(Q2), .in3(Q3), .in4(Q4), .in5(Q5), .in6(Q6), .in7(Q7), .in8(Q8), .in9(Q9),
    .in10(Q10), .in11(Q11), .in12(Q12), .in13(Q13), .in14(Q14), .in15(Q15), .in16(Q16), .in17(Q17),
    .in18(Q18), .in19(Q19), .in20(Q20), .in21(Q21), .in22(Q22), .in23(Q23), .in24(Q24), .in25(Q25),
    .in26(Q26), .in27(Q27), .in28(Q28), .in29(Q29), .in30(Q30), .in31(Q31), .out(D2), .sel(R2));
endmodule
