// Logisim project decode.circ as structural Verilog: 2 circuits, main circuit main
module main (
  input  [31:0] Instruction
);

  wire clock_1_out, RegDst, RegWrite;
  wire [4:0] multiplexer_1_out;
  wire [31:0] De_MemToReg_MUX, imm, R1;

  Clock clock_1 (.out(clock_1_out));
  Multiplexer #(.width(5)) multiplexer_1 (
    .in0(Instruction[20:16]), .in1(Instruction[15:11]), .out(multiplexer_1_out), .sel(RegDst));
  assign imm = {{16{Instruction[15]}}, Instruction[15:0]};  // Bit_Extender bit_extender_1
  registers registers_1 (
    .R1(Instruction[25:21]), .R2(Instruction[20:16]), .WR(multiplexer_1_out), .WD(De_MemToReg_MUX),
    .CLK(clock_1_out), .RegWrite(RegWrite), .D1(R1), .D2(R1));

  // Other names for the same wires on the sheet: funct[5:0] = Instruction[5:0]; opcode[5:0] = Instruction[31:26]

  // Notes on the sheet:
  //   imm
endmodule

module registers (
  input  [4:0] R1,
  input  [4:0] R2,
  input  [4:0] WR,
  input  [31:0] WD,
  input  CLK,
  input  RegWrite,
  output [31:0] D1,
  output [31:0] D2
);

  wire WE1, WE2, WE3, WE4, WE5, WE6, WE7, WE8, WE9, WE10, WE11, WE12, WE13, WE14, WE15, WE16, WE17, WE18,
       WE19, WE20, WE21, WE22, WE23, WE24, WE25, WE26, WE27, WE28, WE29, WE30, WE31;
  wire [31:0] Q0, Q1, Q2, Q3, Q4, Q5, Q6, Q7, Q8, Q9, Q10, Q11, Q12, Q13, Q14, Q15, Q16, Q17, Q18, Q19, Q20,
       Q21, Q22, Q23, Q24, Q25, Q26, Q27, Q28, Q29, Q30, Q31;

  Demultiplexer #(.select(5)) demultiplexer_1 (
    .out1(WE1), .out2(WE2), .out3(WE3), .out4(WE4), .out5(WE5), .out6(WE6), .out7(WE7), .out8(WE8),
    .out9(WE9), .out10(WE10), .out11(WE11), .out12(WE12), .out13(WE13), .out14(WE14), .out15(WE15),
    .out16(WE16), .out17(WE17), .out18(WE18), .out19(WE19), .out20(WE20), .out21(WE21), .out22(WE22),
    .out23(WE23), .out24(WE24), .out25(WE25), .out26(WE26), .out27(WE27), .out28(WE28), .out29(WE29),
    .out30(WE30), .out31(WE31), .in(RegWrite), .sel(WR));  // open: out0
  Register #(.width(32)) zero (.D(WD), .clk(CLK), .Q(Q0));  // open: en, clr
  Register #(.width(32)) a0 (.D(WD), .en(WE4), .clk(CLK), .Q(Q4));  // open: clr
  Register #(.width(32)) t0 (.D(WD), .en(WE8), .clk(CLK), .Q(Q8));  // open: clr
  Register #(.width(32)) t4 (.D(WD), .en(WE12), .clk(CLK), .Q(Q12));  // open: clr
  Register #(.width(32)) s0 (.D(WD), .en(WE16), .clk(CLK), .Q(Q16));  // open: clr
  Register #(.width(32)) s4 (.D(WD), .en(WE20), .clk(CLK), .Q(Q20));  // open: clr
  Register #(.width(32)) t8 (.D(WD), .en(WE24), .clk(CLK), .Q(Q24));  // open: clr
  Register #(.width(32)) gp (.D(WD), .en(WE28), .clk(CLK), .Q(Q28));  // open: clr
  Register #(.width(32)) at (.D(WD), .en(WE1), .clk(CLK), .Q(Q1));  // open: clr
  Register #(.width(32)) a1 (.D(WD), .en(WE5), .clk(CLK), .Q(Q5));  // open: clr
  Register #(.width(32)) t1 (.D(WD), .en(WE9), .clk(CLK), .Q(Q9));  // open: clr
  Register #(.width(32)) t5 (.D(WD), .en(WE13), .clk(CLK), .Q(Q13));  // open: clr
  Register #(.width(32)) s1 (.D(WD), .en(WE17), .clk(CLK), .Q(Q17));  // open: clr
  Register #(.width(32)) s5 (.D(WD), .en(WE21), .clk(CLK), .Q(Q21));  // open: clr
  Register #(.width(32)) t9 (.D(WD), .en(WE25), .clk(CLK), .Q(Q25));  // open: clr
  Register #(.width(32)) sp (.D(WD), .en(WE29), .clk(CLK), .Q(Q29));  // open: clr
  Register #(.width(32)) v0 (.D(WD), .en(WE2), .clk(CLK), .Q(Q2));  // open: clr
  Register #(.width(32)) a2 (.D(WD), .en(WE6), .clk(CLK), .Q(Q6));  // open: clr
  Register #(.width(32)) t2 (.D(WD), .en(WE10), .clk(CLK), .Q(Q10));  // open: clr
  Register #(.width(32)) t6 (.D(WD), .en(WE14), .clk(CLK), .Q(Q14));  // open: clr
  Register #(.width(32)) s2 (.D(WD), .en(WE18), .clk(CLK), .Q(Q18));  // open: clr
  Register #(.width(32)) s6 (.D(WD), .en(WE22), .clk(CLK), .Q(Q22));  // open: clr
  Register #(.width(32)) k0 (.D(WD), .en(WE26), .clk(CLK), .Q(Q26));  // open: clr
  Register #(.width(32)) fp (.D(WD), .en(WE30), .clk(CLK), .Q(Q30));  // open: clr
  Register #(.width(32)) v1 (.D(WD), .en(WE3), .clk(CLK), .Q(Q3));  // open: clr
  Register #(.width(32)) a3 (.D(WD), .en(WE7), .clk(CLK), .Q(Q7));  // open: clr
  Register #(.width(32)) t3 (.D(WD), .en(WE11), .clk(CLK), .Q(Q11));  // open: clr
  Register #(.width(32)) t7 (.D(WD), .en(WE15), .clk(CLK), .Q(Q15));  // open: clr
  Register #(.width(32)) s3 (.D(WD), .en(WE19), .clk(CLK), .Q(Q19));  // open: clr
  Register #(.width(32)) s7 (.D(WD), .en(WE23), .clk(CLK), .Q(Q23));  // open: clr
  Register #(.width(32)) k1 (.D(WD), .en(WE27), .clk(CLK), .Q(Q27));  // open: clr
  Register #(.width(32)) ra (.D(WD), .en(WE31), .clk(CLK), .Q(Q31));  // open: clr
  Multiplexer #(.select(5), .width(32)) multiplexer_1 (
    .in0(Q0), .in1(Q1), .in2(Q2), .in3(Q3), .in4(Q4), .in5(Q5), .in6(Q6), .in7(Q7), .in8(Q8), .in9(Q9),
    .in10(Q10), .in11(Q11), .in12(Q12), .in13(Q13), .in14(Q14), .in15(Q15), .in16(Q16), .in17(Q17),
    .in18(Q18), .in19(Q19), .in20(Q20), .in21(Q21), .in22(Q22), .in23(Q23), .in24(Q24), .in25(Q25),
    .in26(Q26), .in27(Q27), .in28(Q28), .in29(Q29), .in30(Q30), .in31(Q31), .out(D1), .sel(R1));
  Multiplexer #(.select(5), .width(32)) multiplexer_2 (
    .in0(Q0), .in1(Q1), .in2(Q2), .in3(Q3), .in4(Q4), .in5(Q5), .in6(Q6), .in7(Q7), .in8(Q8), .in9(Q9),
    .in10(Q10), .in11(Q11), .in12(Q12), .in13(Q13), .in14(Q14), .in15(Q15), .in16(Q16), .in17(Q17),
    .in18(Q18), .in19(Q19), .in20(Q20), .in21(Q21), .in22(Q22), .in23(Q23), .in24(Q24), .in25(Q25),
    .in26(Q26), .in27(Q27), .in28(Q28), .in29(Q29), .in30(Q30), .in31(Q31), .out(D2), .sel(R2));
endmodule
