// Logisim project execute.circ as structural Verilog: 2 circuits, main circuit main
module alu (
  input  [31:0] A,
  input  [31:0] B,
  input  [3:0] ALUControl,
  output Zero,
  output [31:0] R
);

  wire comparator_1_lt;
  wire [31:0] adder_1_out, and_1_out, bit_extender_1_out, nor_1_out, or_1_out, subtractor_1_out;

  assign and_1_out = A & B;  // AND_Gate and_1, 32 bits wide
  assign or_1_out = A | B;  // OR_Gate or_1, 32 bits wide
  Adder #(.width(32)) adder_1 (.a(A), .b(B), .out(adder_1_out));  // open: cin, cout
  Subtractor #(.width(32)) subtractor_1 (.a(A), .b(B), .out(subtractor_1_out));  // open: bin, bout
  Comparator #(.width(32)) comparator_1 (.a(A), .b(B), .lt(comparator_1_lt));  // open: gt, eq
  assign nor_1_out = ~(A | B);  // NOR_Gate nor_1, 32 bits wide
  assign bit_extender_1_out = {{31{comparator_1_lt}}, comparator_1_lt};  // Bit_Extender bit_extender_1
  Multiplexer #(.select(4), .width(32)) multiplexer_1 (
    .in0(and_1_out), .in1(or_1_out), .in2(adder_1_out), .in6(subtractor_1_out), .in7(bit_extender_1_out),
    .in12(nor_1_out), .out(R), .sel(ALUControl));  // open: in3, in4, in5, in8, in9, in10, in11, in13, in14, in15
  Comparator #(.width(32)) comparator_2 (.a({32{1'b0}}), .b(R), .eq(Zero));  // open: gt, lt
endmodule

module main (
  input  Branch,
  input  [31:0] R1,
  input  [31:0] R2,
  input  [31:0] imm
);

  wire alu_1_zero, and_1_out, DM_p2, MemToReg;
  wire [3:0] ALUCtrl;
  wire [7:0] undriven, undriven_2, undriven_3, undriven_4;
  wire [31:0] adder_1_out, al_PC, alu_1_r, multiplexer_1_out, PC_mas_4, shifter_1_out, WD_RegFile;

  Multiplexer #(.width(32)) multiplexer_1 (.in0(R2), .in1(imm), .out(multiplexer_1_out));  // open: sel
  Shifter #(.width(32)) shifter_1 (.in(imm), .\dist (5'b00010), .out(shifter_1_out));
  Adder #(.width(32)) adder_1 (.a(PC_mas_4), .b(shifter_1_out), .out(adder_1_out));  // open: cin, cout
  alu alu_1 (.A(R1), .B(multiplexer_1_out), .ALUControl(ALUCtrl), .Zero(alu_1_zero), .R(alu_1_r));
  and and_1 (and_1_out, Branch, alu_1_zero);
  // RAM #(.addrWidth(24), .enables("line"), .line("quad")) DM: pin names not known; wires that end beside it: alu_1_r[23:0], DM_p2
  Clock clock_1 (.out(DM_p2));
  Multiplexer #(.width(32)) multiplexer_2 (.in0(PC_mas_4), .in1(adder_1_out), .out(al_PC), .sel(and_1_out));
  Multiplexer #(.width(32)) multiplexer_3 (
    .in0(alu_1_r), .in1({undriven_4, undriven_3, undriven_2, undriven}), .out(WD_RegFile), .sel(MemToReg));
endmodule
