// Logisim project ctrl.circ as structural Verilog: 2 circuits, main circuit main
module main (
  input  [5:0] opcode,
  output out_2,
  output out_3,
  output out_4,
  output out_5,
  output out_6,
  output out_7,
  output out_8,
  output out_9,
  output [1:0] out_10
);

  control control_1 (
    .opcode(opcode), .ALUSrc(out_2), .RegDst(out_3), .MemToReg(out_4), .Jump(out_5), .Branch(out_6),
    .RegWrite(out_7), .MemRead(out_8), .MemWrite(out_9), .ALUOp(out_10));
endmodule

module control (
  input  [5:0] opcode,
  output ALUSrc,
  output RegDst,
  output MemToReg,
  output Jump,
  output Branch,
  output RegWrite,
  output MemRead,
  output MemWrite,
  output [1:0] ALUOp
);

  wire addi_out, ori_out;

  and R (RegDst, ~opcode[5], ~opcode[4], ~opcode[3], ~opcode[2], ~opcode[1], ~opcode[0]);  // AND_Gate
  and lw (MemRead, opcode[5], ~opcode[4], ~opcode[3], ~opcode[2], opcode[1], opcode[0]);  // AND_Gate
  and sw (MemWrite, opcode[5], ~opcode[4], opcode[3], ~opcode[2], opcode[1], opcode[0]);  // AND_Gate
  and beq (Branch, ~opcode[5], ~opcode[4], ~opcode[3], opcode[2], ~opcode[1], ~opcode[0]);  // AND_Gate
  and j (Jump, ~opcode[5], ~opcode[4], ~opcode[3], ~opcode[2], opcode[1], ~opcode[0]);  // AND_Gate
  and addi (addi_out, ~opcode[5], ~opcode[4], opcode[3], ~opcode[2], ~opcode[1], ~opcode[0]);  // AND_Gate
  and ori (ori_out, ~opcode[5], ~opcode[4], opcode[3], opcode[2], ~opcode[1], opcode[0]);  // AND_Gate
  or or_1 (ALUSrc, ori_out, addi_out, MemWrite, MemRead);
  or or_2 (RegWrite, ori_out, addi_out, MemRead, RegDst);
  or or_3 (ALUOp[0], ori_out, Branch);
  or or_4 (ALUOp[1], RegDst, ori_out);

  assign MemToReg = MemRead;
endmodule
