// Logisim project alu_ctrl.circ as structural Verilog
module aluctrl (
  input  [5:0] funct,
  input  [1:0] ALUOp,
  output [3:0] ALUControl
);

  wire [3:0] multiplexer_1_out;

  Multiplexer #(.select(4), .width(4)) multiplexer_1 (
    .in0(4'b0010), .in2(4'b0110), .in4(4'b0000), .in5(4'b0001), .in7(4'b1100), .in10(4'b0111),
    .out(multiplexer_1_out), .sel(funct[3:0]));  // open: in1, in3, in6, in8, in9, in11, in12, in13, in14, in15
  Multiplexer #(.select(2), .width(4)) multiplexer_2 (
    .in0(4'b0010), .in1(4'b0110), .in2(multiplexer_1_out), .in3(4'b0001), .out(ALUControl), .sel(ALUOp));
endmodule
